// Logisim project basic computer.circ as structural Verilog: 17 circuits, main circuit main
module main (
  input  in_1,
  input  in_2,
  input  [3:0] in_3,
  input  [7:0] INPUT_REG,
  output [2:0] out_5,
  output [11:0] AR,
  output [15:0] BUS,
  output [15:0] DR,
  output [15:0] IR,
  output [11:0] PC,
  output [15:0] AC_outp,
  output [15:0] AC_inp,
  output T0,
  output T1,
  output T2,
  output out_16,
  output T4,
  output T5,
  output T6,
  output [7:0] outputr,
  output T7
);

  wire ac_1_add, ac_1_and, ac_1_com, ac_1_dr, ac_1_inpr, ac_1_ld, ac_1_shl, ac_1_shr, and_1_out, and_2_out,
       and_3_out, and_4_out, and_5_out, and_6_out, and_7_out, and_8_out, and_9_out, and_10_out, and_11_out,
       and_12_out, and_13_out, and_14_out, and_15_out, and_16_out, and_17_out, and_18_out, and_19_out,
       and_20_out, and_21_out, and_22_out, and_23_out, and_24_out, and_25_out, and_26_out, and_27_out,
       and_28_out, and_29_out, and_30_out, and_31_out, and_32_out, and_33_out, and_34_out, and_35_out,
       and_36_out, and_37_out, and_38_out, and_39_out, and_40_out, D1T5_out, D5T5_out, D6T6_out,
       decoder_1_out0, decoder_1_out1, decoder_1_out2, decoder_1_out3, decoder_1_out4, decoder_1_out5,
       decoder_1_out6, decoder_1_out7, E_q, E_qn, FGI_q, FGO_q, I_q, I_qn, IEN_q,
       instruction_register_1_ir_0, instruction_register_1_ir_1, instruction_register_1_ir_2,
       instruction_register_1_ir_3, instruction_register_1_ir_4, instruction_register_1_ir_5,
       instruction_register_1_ir_6, instruction_register_1_ir_7, instruction_register_1_ir_8,
       instruction_register_1_ir_9, instruction_register_1_ir_10, instruction_register_1_ir_11,
       instruction_register_1_ir_15, MASTER_CLOCK_out, not_1_out, not_2_out, not_3_out, not_4_out, not_5_out,
       not_6_out, not_7_out, not_8_out, not_9_out, not_10_out, not_11_out, not_12_out, or_1_out, or_2_out,
       or_3_out, or_4_out, or_5_out, or_6_out, or_7_out, or_8_out, or_9_out, or_10_out, or_11_out, R_q, S_q;
  wire [2:0] instruction_register_1_ir_12;
  wire [15:0] ram_1_data, tr_1_output_to_bus;

  and and_1 (and_1_out, decoder_1_out7, I_qn, T4);
  and and_2 (and_2_out, decoder_1_out7, I_qn, out_16);
  Decoder #(.select(3), .enable("false")) decoder_1 (
    .out0(decoder_1_out0), .out1(decoder_1_out1), .out2(decoder_1_out2), .out3(decoder_1_out3),
    .out4(decoder_1_out4), .out5(decoder_1_out5), .out6(decoder_1_out6), .out7(decoder_1_out7),
    .sel(instruction_register_1_ir_12));
  and and_3 (and_3_out, decoder_1_out5, T4);
  and and_4 (and_4_out, and_39_out, instruction_register_1_ir_6);
  and and_5 (and_5_out, R_q, T2);
  not not_1 (not_1_out, R_q);
  and and_6 (and_6_out, T2, not_2_out);
  not not_2 (not_2_out, R_q);
  and and_7 (and_7_out, and_39_out, instruction_register_1_ir_7);
  or or_1 (or_1_out, and_4_out, and_5_out);
  not not_3 (not_3_out, and_8_out);
  and and_8 (and_8_out, and_39_out, instruction_register_1_ir_11);
  not not_4 (not_4_out, and_9_out);
  and and_9 (and_9_out, and_39_out, instruction_register_1_ir_10);
  and and_10 (and_10_out, T2, not_1_out, instruction_register_1_ir_15);
  not not_5 (not_5_out, and_10_out);
  or or_2 (or_2_out, and_9_out, and_16_out);
  J_K_Flip_Flop FGI (.J(and_8_out), .clk(MASTER_CLOCK_out), .K(not_3_out), .Q(FGI_q));  // open: Qn, preset, en, reset
  J_K_Flip_Flop FGO (.J(and_9_out), .clk(MASTER_CLOCK_out), .K(not_4_out), .Q(FGO_q));  // open: Qn, preset, en, reset
  J_K_Flip_Flop I (
    .J(and_10_out), .clk(MASTER_CLOCK_out), .K(not_5_out), .Q(I_q), .Qn(I_qn));  // open: preset, en, reset
  and and_11 (and_11_out, and_2_out, instruction_register_1_ir_0);
  J_K_Flip_Flop IEN (.J(and_7_out), .clk(MASTER_CLOCK_out), .K(or_1_out), .Q(IEN_q));  // open: Qn, preset, en, reset
  or or_3 (or_3_out, FGI_q, FGO_q);
  J_K_Flip_Flop S (.J(not_6_out), .clk(MASTER_CLOCK_out), .K(and_11_out), .Q(S_q));  // open: Qn, preset, en, reset
  not not_6 (not_6_out, and_11_out);
  and and_12 (and_12_out, decoder_1_out2, T5);
  and and_13 (and_13_out, R_q, T0);
  and and_14 (and_14_out, T2, T1);
  not not_7 (not_7_out, T1);
  and D5T5 (D5T5_out, decoder_1_out5, T6);
  and and_15 (and_15_out, R_q, T1);
  and and_16 (and_16_out, T4, decoder_1_out3);
  and and_17 (and_17_out, decoder_1_out6, T6);
  or or_4 (or_4_out, and_17_out, and_12_out);
  not not_8 (not_8_out, T2);
  and and_18 (and_18_out, MASTER_CLOCK_out, S_q);
  or or_5 (or_5_out, and_15_out, and_16_out, and_3_out, and_17_out);
  and and_19 (and_19_out, and_2_out, AC_inp[15], instruction_register_1_ir_6);
  and and_20 (and_20_out, and_2_out, instruction_register_1_ir_10);
  and and_21 (and_21_out, and_2_out, E_qn, instruction_register_1_ir_8);
  and and_22 (and_22_out, and_2_out, AC_inp[0], instruction_register_1_ir_7);
  and and_23 (and_23_out, or_3_out, IEN_q, T0, not_7_out, not_8_out);
  and and_24 (and_24_out, out_16, R_q);
  and D6T6 (D6T6_out, decoder_1_out6, T7);
  and and_25 (and_25_out, T0, not_9_out);
  not not_9 (not_9_out, R_q);
  not not_10 (not_10_out, decoder_1_out7);
  and and_26 (and_26_out, decoder_1_out1, T5);
  or or_6 (or_6_out, and_19_out, and_20_out, and_21_out, and_22_out, and_26_out);
  J_K_Flip_Flop R (.J(and_23_out), .clk(MASTER_CLOCK_out), .K(and_24_out), .Q(R_q));  // open: Qn, preset, en, reset
  and and_27 (and_27_out, T5, decoder_1_out3);
  and and_28 (and_28_out, not_9_out, T1);
  and and_29 (and_29_out, not_10_out, I_q, out_16);
  and and_30 (and_30_out, decoder_1_out0, T4);
  and and_31 (and_31_out, decoder_1_out1, T4);
  and and_32 (and_32_out, decoder_1_out2, T4);
  J_K_Flip_Flop #(.trigger("falling")) E (
    .J(or_6_out), .clk(MASTER_CLOCK_out), .K(not_11_out), .Q(E_q), .Qn(E_qn));  // open: preset, en, reset
  not not_11 (not_11_out, or_6_out);
  and and_33 (and_33_out, decoder_1_out6, T4);
  SC sc_1 (
    .B0(instruction_register_1_ir_0), .Clock(and_18_out), .D7I_prime_T3(and_1_out), .D7IT3(and_38_out),
    .RT2(and_24_out), .D0T6(and_35_out), .D1T5(D1T5_out), .D2T6(and_37_out), .D3T5(and_27_out),
    .D4T5(and_36_out), .D5T5(D5T5_out), .D6T6(D6T6_out), .T0(T0), .T1(T1), .T2(T2), .T3(out_16), .T4(T4),
    .T5(T5), .T6(T6), .T7(T7));  // open: T8, T9, T10, T11, T12, T13, T14, T15
  or or_7 (or_7_out, and_13_out, and_3_out, and_25_out);
  or or_8 (or_8_out, and_28_out, and_29_out, and_30_out, and_31_out, and_32_out, and_33_out);
  and D1T5 (D1T5_out, T5, T6);
  and and_34 (and_34_out, T4, decoder_1_out4);
  and and_35 (and_35_out, T6, decoder_1_out0);
  and and_36 (and_36_out, decoder_1_out4, T6);
  and and_37 (and_37_out, T6, decoder_1_out2);
  DR dr_1 (
    .input_16_bits_from_bus(BUS), .T4(T4), .T5(T5), .D0(decoder_1_out0), .D1(decoder_1_out1),
    .D2(decoder_1_out2), .D6(decoder_1_out6), .CLOCK(MASTER_CLOCK_out), .OUTPUT_TO__BUS(DR));
  and and_38 (and_38_out, T4, decoder_1_out7, I_q);
  RAM #(.addrWidth(12), .dataWidth(16), .bus("separate")) ram_1 (
    .addr(AR), .din(BUS), .data(ram_1_data), .str(or_5_out), .sel(1'b1), .clk(MASTER_CLOCK_out), .ld(or_8_out));  // open: clr
  Address_register_AR address_register_ar_1 (
    .input_12_bits_from_bus(BUS[11:0]), .R(R_q), .D5(decoder_1_out5), .I(I_q), .D7(decoder_1_out7), .T0(T0),
    .T2(T2), .T3(out_16), .T4(T4), .clock(MASTER_CLOCK_out), .output_of_AR(AR));
  TR tr_1 (
    .input_16_bits_from_bus(BUS), .I(I_q), .D7(decoder_1_out7), .T3(out_16), .T0(T0), .CLK(MASTER_CLOCK_out),
    .OUTPUT_TO_BUS(tr_1_output_to_bus));
  OUTR outr_1 (
    .input_8_bits_from_bus(BUS[7:0]), .d7(decoder_1_out7), .I(I_q), .T3(out_16),
    .B10(instruction_register_1_ir_10), .CLOCK(MASTER_CLOCK_out), .OUTPUT(outputr));
  and and_39 (and_39_out, decoder_1_out7, I_q, out_16);
  and and_40 (and_40_out, T5, decoder_1_out5);
  PC pc_1 (
    .input_12_bits_from_bus(BUS[11:0]), .D4(decoder_1_out4), .D5(decoder_1_out5), .D6(decoder_1_out6),
    .D7(decoder_1_out7), .I(I_q), .R(R_q), .T1(T1), .B1(instruction_register_1_ir_2), .T2(T2),
    .B2(instruction_register_1_ir_3), .T3(out_16), .B3(instruction_register_1_ir_1), .T4(T4),
    .B4(instruction_register_1_ir_4), .T5(T5), .T6(T6), .B8(instruction_register_1_ir_8),
    .B9(instruction_register_1_ir_9), .AC_15(AC_inp[15]), .FGI(FGI_q), .FGO(FGO_q), .AC(or_10_out),
    .DR(not_12_out), .CLOCK(MASTER_CLOCK_out), .OUTPUT_TO_BUS(PC));
  AC ac_1 (
    .input__16bits__from_ALU(AC_outp), .T6(T6), .T3(out_16), .T5(T5), .D0(decoder_1_out0),
    .D1(decoder_1_out1), .D2(decoder_1_out2), .D7(decoder_1_out7), .B5(instruction_register_1_ir_5),
    .B6(instruction_register_1_ir_6), .B7(instruction_register_1_ir_7), .B9(instruction_register_1_ir_9),
    .B11(instruction_register_1_ir_11), .I(I_q), .CLK(MASTER_CLOCK_out), .INPR(ac_1_inpr), .LD(ac_1_ld),
    .AND(ac_1_and), .ADD(ac_1_add), .DR(ac_1_dr), .input__16bits__from_ALU_2(AC_inp), .COM(ac_1_com),
    .SHR(ac_1_shr), .SHL(ac_1_shl));
  or or_9 (or_9_out, and_34_out, and_40_out);
  BUS bus_1 (
    .AR(AR), .DR(DR), .AC(AC_inp), .IR(IR), .TR(tr_1_output_to_bus), .MEMORY(ram_1_data), .in_10(out_5),
    .TO_REGISTERS(BUS), .in_2(in_3), .PC(PC), .extra(in_3));
  INSTRUCTION_REGISTER instruction_register_1 (
    .INPUT_16_BIT(BUS), .R(R_q), .T1(T1), .IR_15(instruction_register_1_ir_15),
    .IR_14(instruction_register_1_ir_12[2]), .IR_13(instruction_register_1_ir_12[1]),
    .IR_12(instruction_register_1_ir_12[0]), .IR_11(instruction_register_1_ir_11),
    .IR_10(instruction_register_1_ir_10), .IR_9(instruction_register_1_ir_9),
    .IR_8(instruction_register_1_ir_8), .IR_7(instruction_register_1_ir_7),
    .IR_6(instruction_register_1_ir_6), .IR_5(instruction_register_1_ir_5),
    .IR_4(instruction_register_1_ir_4), .IR_1(instruction_register_1_ir_1),
    .IR_3(instruction_register_1_ir_3), .IR_2(instruction_register_1_ir_2),
    .IR_0(instruction_register_1_ir_0), .CLK(MASTER_CLOCK_out), .OUTPUT_16_BIT(IR));  // open: CLR
  Clock MASTER_CLOCK (.out(MASTER_CLOCK_out));
  ALU alu_1 (
    .AC_reg(AC_inp), .clk(MASTER_CLOCK_out), .AND(ac_1_and), .inpr(ac_1_inpr), .shr(ac_1_shr),
    .shl(ac_1_shl), .DR(ac_1_dr), .ADD(ac_1_add), .com(ac_1_com), .LD(ac_1_ld), .E(E_q), .to_AC(AC_outp),
    .DR_Reg(DR), .INP_reg(INPUT_REG));
  // Priority_Encoder priority_encoder_1: pin names not known; wires that end beside it: out_5, in_2, in_1, or_9_out, or_7_out, or_4_out, or_2_out, and_6_out, and_14_out, or_8_out
  or or_10 (or_10_out, AC_inp[0], AC_inp[1], AC_inp[2], AC_inp[3], AC_inp[4], AC_inp[5], AC_inp[6], AC_inp[7], AC_inp[8], AC_inp[9], AC_inp[10], AC_inp[11], AC_inp[12], AC_inp[13], AC_inp[14], AC_inp[15]);
  not not_12 (not_12_out, or_11_out);
  or or_11 (or_11_out, DR[0], DR[1], DR[2], DR[3], DR[4], DR[5], DR[6], DR[7], DR[8], DR[9], DR[10], DR[11], DR[12], DR[13], DR[14], DR[15]);

  // Notes on the sheet:
  //   r
  //   D76543210
  //   p
  //   B6
  //   R
  //   T2
  //   p
  //   B11
  //   p
  //   B10
  //   T2
  //   R'
  //   p
  //   B7
  //   IR(15)
  //   R'T2
  //   FGI
  //   FGO
  //   r
  //   B0
  //   R
  //   T1
  //   T4
  //   D3
  //   D6
  //   T6
  //   RT1
  //   FGI+FGO
  //   IEN
  //   T0
  //   T1'
  //   T2'
  //   T3
  //   R
  //   r
  //   B6
  //   r
  //   B10
  //   r
  //   E'
  //   B8
  //   r
  //   B7
  //   R'
  //   T1
  //   T4
  //   rB6
  //   rB10
  //   rB8
  //   rB7
  //   D1T5
  //   D6
  //   D0T6
  //   D4T4
  //   WRITE
  //   READ
  //   p
  //   READ
  //   check if AC==0 return 1 if AC!=0, return 0 if AC ==0
  //   0000 0011 0101 0011
  //   0110 1000 1000 1000
endmodule

module registers (
  input  [11:0] input_12_bits_from_bus,
  input  D7,
  input  I,
  input  T3,
  input  T2,
  input  R,
  input  T0,
  input  D5,
  input  T4,
  input  in_10,
  output output_of_AR
);

  wire AC_carry, ADD_out, and_2_out, and_3_out, and_4_out, and_5_out, and_6_out, and_7_out, and_8_out,
       and_9_out, and_10_out, and_11_out, and_12_out, and_13_out, and_14_out, and_15_out, and_16_out,
       and_17_out, and_18_out, and_19_out, and_20_out, and_21_out, and_22_out, AND_out, CLR_2_out, CLR_3_out,
       CLR_out, COM_out, DR_2_carry, DR_out, IEN_q, INC_out, INCR_2_out, INCR_3_out, INCR_out, INPR_out,
       IR_carry, LD_2_out, LD_3_out, LD_out, LOAD_2_out, LOAD_3_out, LOAD_out, not_1_out, not_2_out,
       or_1_out, or_2_out, PC_carry, SHL_out, SHR_out, TR_carry, undriven, undriven_2, undriven_3,
       undriven_4, undriven_5, undriven_6, undriven_7, undriven_8, undriven_9, undriven_10, undriven_11,
       undriven_12, undriven_13, undriven_14, undriven_15, undriven_16, undriven_17, undriven_18,
       undriven_21, undriven_22, undriven_24, undriven_25, undriven_26, undriven_27, undriven_28,
       undriven_29, undriven_30, undriven_31, undriven_32, undriven_33, undriven_34, undriven_35,
       undriven_36, undriven_37, undriven_38, undriven_39, undriven_40, undriven_41, undriven_42,
       undriven_43, undriven_44, undriven_45, undriven_46, undriven_47, undriven_48, undriven_49,
       undriven_50, undriven_51, undriven_55, undriven_56, undriven_57, undriven_58, undriven_59;
  wire [7:0] undriven_23;
  wire [11:0] undriven_54;
  wire [15:0] undriven_19, undriven_20, undriven_52, undriven_53;

  not not_1 (not_1_out, R);
  and AND (AND_out, undriven, undriven_2);
  and ADD (ADD_out, undriven_3, undriven_2);
  and DR (DR_out, undriven_4, undriven_2);
  and INPR (INPR_out, undriven_5, undriven_6);
  and COM (COM_out, undriven_7, undriven_8);
  and SHR (SHR_out, undriven_7, undriven_9);
  and SHL (SHL_out, undriven_7, undriven_10);
  and INC (INC_out, undriven_7, undriven_11);
  and CLR (CLR_out, undriven_7, undriven_12);
  and and_2 (and_2_out, undriven_13, undriven_14);
  and and_3 (and_3_out, undriven_15, undriven_14);
  and and_4 (and_4_out, undriven_14, undriven_16);
  and and_5 (and_5_out, undriven_14, undriven_17);
  and INCR (INCR_out, undriven_17, undriven_18);
  and and_6 (and_6_out, D7, I, T3);
  and and_7 (and_7_out, T2, not_1_out);
  and and_8 (and_8_out, not_1_out, T0);
  and INCR_2 (INCR_2_out, D5, T4);
  and CLR_2 (CLR_2_out, T0, R);
  or LD (LD_out, and_2_out, and_3_out, and_4_out, and_5_out);
  or LD_2 (LD_2_out, and_6_out, and_7_out, and_8_out);
  or or_1 (or_1_out, AND_out, ADD_out, DR_out, INPR_out, COM_out, SHR_out, SHL_out);
  Counter #(.width(16), .max('hffff)) AC (
    .load(or_1_out), .D(undriven_20), .count(INC_out), .carry(AC_carry), .clr(CLR_out));  // open: Q, clk
  Counter #(.width(16), .max('hffff)) DR_2 (
    .load(LD_out), .D(undriven_19), .count(INCR_out), .carry(DR_2_carry));  // open: Q, clk, clr
  Counter #(.width(12), .max('hfff)) AR (
    .load(LD_2_out), .D(input_12_bits_from_bus), .count(INCR_2_out), .carry(output_of_AR), .clr(CLR_2_out));  // open: Q, clk
  and LOAD (LOAD_out, undriven_21, undriven_22);
  Register OUTR (.D(undriven_23), .en(LOAD_out));  // open: Q, clk, clr
  and LOAD_2 (LOAD_2_out, undriven_24, undriven_25);
  and LOAD_3 (LOAD_3_out, undriven_26, undriven_27);
  not not_2 (not_2_out, undriven_28);
  and and_9 (and_9_out, not_2_out, undriven_29);
  and and_10 (and_10_out, undriven_28, undriven_30);
  and and_11 (and_11_out, undriven_31, undriven_32, undriven_33);
  and and_12 (and_12_out, undriven_34, undriven_35, undriven_36);
  and and_13 (and_13_out, undriven_34, undriven_37, undriven_38);
  and and_14 (and_14_out, undriven_34, undriven_39, undriven_40);
  and and_15 (and_15_out, undriven_41, undriven_42, undriven_43);
  and and_16 (and_16_out, undriven_41, undriven_44, undriven_45);
  and and_17 (and_17_out, undriven_34, undriven_46, undriven_47);
  Counter #(.width(16), .max('hffff)) TR (
    .load(LOAD_2_out), .D(undriven_52), .carry(TR_carry));  // open: count, Q, clk, clr
  Counter #(.width(16), .max('hffff)) IR (
    .load(LOAD_3_out), .D(undriven_53), .carry(IR_carry));  // open: count, Q, clk, clr
  and and_18 (and_18_out, undriven_48, undriven_49);
  and and_19 (and_19_out, undriven_50, undriven_51);
  and CLR_3 (CLR_3_out, undriven_28, undriven_29);
  or LD_3 (LD_3_out, and_18_out, and_19_out);
  Counter #(.width(12), .max('hfff)) PC (
    .load(LD_3_out), .D(undriven_54), .count(INCR_3_out), .carry(PC_carry), .clr(CLR_3_out));  // open: Q, clk
  or INCR_3 (INCR_3_out, and_9_out, and_10_out, and_11_out, and_12_out, and_13_out, and_14_out, and_15_out, and_16_out, and_17_out);
  and and_20 (and_20_out, undriven_55, undriven_57);
  and and_21 (and_21_out, undriven_58, undriven_59);
  and and_22 (and_22_out, undriven_55, undriven_56);
  or or_2 (or_2_out, and_20_out, and_21_out);
  J_K_Flip_Flop IEN (.J(and_22_out), .K(or_2_out), .Q(IEN_q), .en(in_10));  // open: clk, Qn, preset, reset

  // Notes on the sheet:
  //   D0
  //   T5
  //   D1
  //   D2
  //   p
  //   B11
  //   r
  //   B9
  //   B7
  //   B6
  //   B5
  //   B11
  //   D0
  //   T4
  //   D1
  //   D2
  //   D6
  //   T5
  //   input 16 bits from bus
  //   input (16bits) from ALU
  //   to bus
  //   p
  //   B10
  //   input 8 bits from bus
  //   r
  //   T0
  //   R'
  //   T1
  //   D4
  //   T4
  //   D5
  //   T5
  //   R
  //   T1
  //   T2
  //   D6
  //   T6
  //   DR
  //   r
  //   B4
  //   AC(15)'
  //   B3
  //   AC(15)
  //   B2
  //   AC'
  //   p
  //   B9
  //   FGI
  //   B8
  //   FGO
  //   B1
  //   E'
  //   input 16 bits from bus
  //   input 16 bits from bus
  //   input 12 bits from bus
  //   p
  //   B7
  //   B6
  //   R
  //   T2
endmodule

// AR
module Address_register_AR (
  input  [11:0] input_12_bits_from_bus,
  input  I,
  input  D7,
  input  R,
  input  D5,
  input  T3,
  input  T0,
  input  T2,
  input  T4,
  input  clock,
  output [11:0] output_of_AR
);

  wire and_1_out, and_2_out, and_3_out, CLR_out, INCR_out, LD_out, not_1_out, not_2_out;

  not not_1 (not_1_out, D7);
  not not_2 (not_2_out, R);
  and CLR (CLR_out, T0, R);
  and and_1 (and_1_out, not_1_out, I, T3);
  and and_2 (and_2_out, T2, not_2_out);
  and and_3 (and_3_out, not_2_out, T0);
  and INCR (INCR_out, D5, T4);
  or LD (LD_out, and_1_out, and_2_out, and_3_out);
  Counter #(.width(12), .max('hfff)) AR (
    .load(LD_out), .D(input_12_bits_from_bus), .count(INCR_out), .Q(output_of_AR), .clk(clock), .clr(CLR_out));  // open: carry
endmodule

module PC (
  input  [11:0] input_12_bits_from_bus,
  input  D4,
  input  D5,
  input  D6,
  input  D7,
  input  T1,
  input  T2,
  input  T3,
  input  T4,
  input  T5,
  input  T6,
  input  I,
  input  CLOCK,
  input  FGI,
  input  FGO,
  input  R,
  input  DR,
  input  AC,
  input  B1,
  input  B2,
  input  B3,
  input  B4,
  input  B8,
  input  B9,
  input  AC_15,
  output [11:0] OUTPUT_TO_BUS
);

  wire and_1_out, and_2_out, and_3_out, and_4_out, and_5_out, and_6_out, and_7_out, and_8_out, and_9_out,
       and_10_out, and_11_out, and_12_out, and_13_out, CLR_out, INCR_out, LD_out, not_1_out, not_2_out,
       not_3_out, not_4_out;

  and and_1 (and_1_out, D7, T3, I);
  and and_2 (and_2_out, D7, not_1_out, T3);
  not not_1 (not_1_out, I);
  not not_2 (not_2_out, AC_15);
  not not_3 (not_3_out, R);
  not not_4 (not_4_out, AC);
  and and_3 (and_3_out, D4, T4);
  and and_4 (and_4_out, D5, T5);
  and and_5 (and_5_out, not_3_out, T1);
  and and_6 (and_6_out, R, T2);
  and and_7 (and_7_out, D6, T6, DR);
  and and_8 (and_8_out, and_2_out, B4, not_2_out);
  and and_9 (and_9_out, and_2_out, B3, AC_15);
  and and_10 (and_10_out, and_2_out, B2, not_4_out);
  and and_11 (and_11_out, and_1_out, B9, FGI);
  and and_12 (and_12_out, and_1_out, B8, FGO);
  and and_13 (and_13_out, and_2_out, B1, FGO);
  and CLR (CLR_out, R, T1);
  or LD (LD_out, and_3_out, and_4_out);
  or INCR (INCR_out, and_5_out, and_6_out, and_7_out, and_8_out, and_9_out, and_10_out, and_11_out, and_12_out, and_13_out);
  Counter #(.width(12), .max('hfff)) PC (
    .load(LD_out), .D(input_12_bits_from_bus), .count(INCR_out), .Q(OUTPUT_TO_BUS), .clk(CLOCK), .clr(CLR_out));  // open: carry
endmodule

module DR (
  input  [15:0] input_16_bits_from_bus,
  input  CLOCK,
  input  T4,
  input  T5,
  input  D0,
  input  D1,
  input  D2,
  input  D6,
  output [15:0] OUTPUT_TO__BUS
);

  wire and_1_out, and_2_out, and_3_out, and_4_out, INCR_out, LD_out;

  and and_1 (and_1_out, D0, T4);
  and and_2 (and_2_out, D1, T4);
  and and_3 (and_3_out, T4, D2);
  and and_4 (and_4_out, T4, D6);
  and INCR (INCR_out, D6, T5);
  or LD (LD_out, and_1_out, and_2_out, and_3_out, and_4_out);
  Counter #(.width(16), .max('hffff)) DR (
    .load(LD_out), .D(input_16_bits_from_bus), .count(INCR_out), .Q(OUTPUT_TO__BUS), .clk(CLOCK));  // open: carry, clr
endmodule

module OUTR (
  input  [7:0] input_8_bits_from_bus,
  input  B10,
  input  T3,
  input  d7,
  input  I,
  input  CLOCK,
  output [7:0] OUTPUT
);

  wire and_1_out, LOAD_out;

  and and_1 (and_1_out, d7, I, T3);
  and LOAD (LOAD_out, and_1_out, B10);
  Register OUTR (.D(input_8_bits_from_bus), .en(LOAD_out), .Q(OUTPUT), .clk(CLOCK));  // open: clr

  // Notes on the sheet:
  //   p
  //   B10
endmodule

// IR
module INSTRUCTION_REGISTER (
  input  [15:0] INPUT_16_BIT,
  input  R,
  input  CLK,
  input  T1,
  input  CLR,
  output [15:0] OUTPUT_16_BIT,
  output IR_0,
  output IR_15,
  output IR_1,
  output IR_14,
  output IR_13,
  output IR_11,
  output IR_10,
  output IR_9,
  output IR_8,
  output IR_12,
  output IR_2,
  output IR_7,
  output IR_6,
  output IR_5,
  output IR_4,
  output IR_3
);

  wire and_1_out, not_1_out;

  not not_1 (not_1_out, R);
  and and_1 (and_1_out, not_1_out, T1);
  Register #(.width(16)) register_1 (
    .D(INPUT_16_BIT), .en(and_1_out),
    .Q({IR_15, IR_14, IR_13, IR_12, IR_11, IR_10, IR_9, IR_8, IR_7, IR_6, IR_5, IR_4, IR_3, IR_2, IR_1, IR_0}),
    .clk(CLK), .clr(CLR));

  assign OUTPUT_16_BIT = {IR_15, IR_14, IR_13, IR_12, IR_11, IR_10, IR_9, IR_8, IR_7, IR_6, IR_5, IR_4, IR_3, IR_2, IR_1, IR_0};
endmodule

// I FF
module I_FLIP_FLOP (
  input  CLK,
  input  R,
  input  T1,
  input  T2,
  input  FGI,
  output I_BIT
);

  wire and_1_out, and_2_out, not_1_out, not_2_out, not_3_out, or_1_out;

  and and_1 (and_1_out, R, T1);
  not not_1 (not_1_out, R);
  and and_2 (and_2_out, not_1_out, T2);
  or or_1 (or_1_out, and_1_out, and_2_out, FGI);
  not not_2 (not_2_out, or_1_out);
  D_Flip_Flop I (.clk(CLK), .D(not_2_out), .Q(I_BIT), .en(not_3_out));  // open: Qn, preset, reset
  not not_3 (not_3_out, 1'b1);
endmodule

// R FF
module R_FLIP_FLOP (
  input  CLK,
  input  FGI,
  input  FGO,
  input  IEN,
  input  I,
  input  D7,
  input  T3,
  output R
);

  wire and_1_out, and_2_out, not_1_out, or_1_out;

  or or_1 (or_1_out, FGI, FGO);
  and and_1 (and_1_out, I, D7, T3);
  and and_2 (and_2_out, or_1_out, IEN, and_1_out);
  not not_1 (not_1_out, 1'b1);
  D_Flip_Flop u_R (.clk(CLK), .D(and_2_out), .Q(R), .en(not_1_out));  // open: Qn, preset, reset
endmodule

// E FF
module E_FLIP_FLOP (
  input  CLK,
  input  T2_prime,
  input  R,
  output E_FF
);

  wire and_1_out, not_1_out, not_2_out;

  and and_1 (and_1_out, T2_prime, R);
  D_Flip_Flop E (.clk(CLK), .D(not_1_out), .Q(E_FF), .en(not_2_out));  // open: Qn, preset, reset
  not not_1 (not_1_out, and_1_out);
  not not_2 (not_2_out, 1'b1);

  // Notes on the sheet:
  //   R
  //   T2'
endmodule

// IEN FF
module IEN_FLIP_FLOP (
  input  CLK,
  input  I,
  input  D7,
  input  T3,
  input  B7,
  input  B6,
  input  R,
  input  T2,
  output IEN
);

  wire and_1_out, and_2_out, and_3_out, and_4_out, not_1_out, or_1_out;

  and and_1 (and_1_out, I, D7, T3);
  and and_2 (and_2_out, and_1_out, B7);
  and and_3 (and_3_out, and_1_out, B6);
  or or_1 (or_1_out, and_3_out, and_4_out);
  and and_4 (and_4_out, R, T2);
  J_K_Flip_Flop u_IEN (.J(and_2_out), .clk(CLK), .K(or_1_out), .Q(IEN), .en(not_1_out));  // open: Qn, preset, reset
  not not_1 (not_1_out, 1'b1);

  // Notes on the sheet:
  //   B7
  //   p
  //   B6
  //   R
  //   T2
endmodule

module TR (
  input  [15:0] input_16_bits_from_bus,
  input  D7,
  input  I,
  input  CLK,
  input  T0,
  input  T3,
  output [15:0] OUTPUT_TO_BUS
);

  wire and_1_out, LOAD_out, not_1_out;

  not not_1 (not_1_out, I);
  and and_1 (and_1_out, D7, not_1_out, T3);
  and LOAD (LOAD_out, and_1_out, T0);
  Counter #(.width(16), .max('hffff)) TR (
    .load(LOAD_out), .D(input_16_bits_from_bus), .Q(OUTPUT_TO_BUS), .clk(CLK));  // open: count, carry, clr

  // Notes on the sheet:
  //   r
endmodule

module AC (
  input  [15:0] input__16bits__from_ALU,
  input  D0,
  input  D1,
  input  D2,
  input  D7,
  input  T3,
  input  T5,
  input  T6,
  input  CLK,
  input  B5,
  input  B6,
  input  B7,
  input  B9,
  input  B11,
  input  I,
  output INPR,
  output LD,
  output AND,
  output ADD,
  output DR,
  output [15:0] input__16bits__from_ALU_2,
  output COM,
  output SHR,
  output SHL
);

  wire and_1_out, and_2_out, and_3_out, CLR_out, INC_out, not_1_out;

  and and_1 (and_1_out, D2, T6);
  and and_2 (and_2_out, D7, T3, I);
  and and_3 (and_3_out, D7, T3, not_1_out);
  not not_1 (not_1_out, I);
  and AND_4 (AND, D0, T5);
  and u_ADD (ADD, D1, T5);
  and u_DR (DR, D2, T5);
  and u_INPR (INPR, and_2_out, B11);
  and u_COM (COM, and_3_out, B9);
  and u_SHR (SHR, and_3_out, B7);
  and u_SHL (SHL, and_3_out, B6);
  and INC (INC_out, and_3_out, B5);
  and CLR (CLR_out, and_3_out, B11);
  or or_1 (LD, AND, ADD, DR, INPR, SHR, SHL, COM, and_1_out);
  Counter #(.width(16), .max('hffff)) AC (
    .load(LD), .D(input__16bits__from_ALU), .count(INC_out), .Q(input__16bits__from_ALU_2), .clk(CLK),
    .clr(CLR_out));  // open: carry

  // Notes on the sheet:
  //   T5
  //   r
  //   0010 0011 0100 0101
  //   0010 0000 0000 0001
  //   0010 0000 0000 0001
endmodule

module BUS (
  input  [11:0] AR,
  input  [3:0] in_2,
  input  [11:0] PC,
  input  [3:0] extra,
  input  [15:0] DR,
  input  [15:0] AC,
  input  [15:0] IR,
  input  [15:0] TR,
  input  [15:0] MEMORY,
  input  [2:0] in_10,
  output [15:0] TO_REGISTERS
);

  Multiplexer #(.select(3), .width(16), .enable("false")) multiplexer_1 (
    .in0({16{1'b0}}), .in1({in_2, AR}), .in2({extra, PC}), .in3(DR), .in4(AC), .in5(IR), .in6(TR),
    .in7(MEMORY), .out(TO_REGISTERS), .sel(in_10));

  // Notes on the sheet:
  //   FROM REGISTERS
  //   TO REGISTERS
  //   BUS 
  //   15    14    13   12   11    10    9     8      7      6      5      4     3     2     1     0
endmodule

module ALU_stage1 (
  input  AC_i,
  input  AND,
  input  ADD,
  input  DR,
  input  DR_i,
  input  LD,
  input  INPR,
  input  INPR_i,
  input  COM,
  input  CLK,
  input  SHR,
  input  AC_i_1,
  input  SHL,
  input  AC_i_1_2,
  output \output 
);

  wire adder_1_cout, adder_1_out, and_1_out, and_2_out, and_3_out, and_4_out, and_5_out, and_6_out,
       and_7_out, and_8_out, and_9_out, not_1_out, not_2_out, or_1_out, undriven;

  Adder #(.width(1)) adder_1 (.a(AC_i), .b(DR_i), .out(adder_1_out), .cin(undriven), .cout(adder_1_cout));
  not not_1 (not_1_out, AC_i);
  and and_1 (and_1_out, AND, AC_i, DR_i);
  and and_2 (and_2_out, ADD, adder_1_out);
  and and_3 (and_3_out, DR, DR_i);
  and and_4 (and_4_out, INPR, INPR_i);
  and and_5 (and_5_out, COM, not_1_out);
  and and_6 (and_6_out, SHR, AC_i_1);
  and and_7 (and_7_out, SHL, AC_i_1_2);
  or or_1 (or_1_out, and_1_out, and_2_out, and_3_out, and_4_out, and_5_out, and_6_out, and_7_out);
  not not_2 (not_2_out, or_1_out);
  and and_8 (and_8_out, LD, or_1_out);
  and and_9 (and_9_out, not_2_out, LD);
  J_K_Flip_Flop j_k_ff_1 (.J(and_8_out), .clk(CLK), .K(and_9_out), .Q(\output ));  // open: Qn, preset, en, reset

  // Notes on the sheet:
  //   AND
  //   ADD
  //   INPR
  //   INPR(i bit)
  //   COM
  //   SHR
  //   AC(i+!)
  //   SHL
  //   AC(i-1)
  //   DR
  //   LD
endmodule

module ALU (
  input  [15:0] AC_reg,
  input  clk,
  input  AND,
  input  inpr,
  input  shr,
  input  shl,
  input  DR,
  input  [15:0] DR_Reg,
  input  E,
  input  ADD,
  input  com,
  input  LD,
  input  [7:0] INP_reg,
  output [15:0] to_AC
);

  wire not_1_out, undriven, undriven_2, undriven_3, undriven_4, undriven_5, undriven_6, undriven_7,
       undriven_8;

  not not_1 (not_1_out, 1'b1);
  ALU_stage1 _15 (
    .AC_i(AC_reg[15]), .AND(AND), .DR_i(DR_Reg[15]), .LD(LD), .INPR(inpr), .INPR_i(undriven_2), .COM(com),
    .CLK(clk), .SHR(shr), .AC_i_1(E), .SHL(shl), .AC_i_1_2(AC_reg[14]), .ADD(ADD), .DR(DR),
    .\output (to_AC[15]));
  ALU_stage1 _11 (
    .AC_i(AC_reg[11]), .AND(AND), .DR_i(DR_Reg[11]), .LD(LD), .INPR(inpr), .INPR_i(undriven), .COM(com),
    .CLK(clk), .SHR(shr), .AC_i_1(AC_reg[12]), .SHL(shl), .AC_i_1_2(AC_reg[10]), .ADD(ADD), .DR(DR),
    .\output (to_AC[11]));
  ALU_stage1 _7 (
    .AC_i(AC_reg[7]), .AND(AND), .DR_i(DR_Reg[7]), .LD(LD), .INPR(inpr), .INPR_i(INP_reg[7]), .COM(com),
    .CLK(clk), .SHR(shr), .AC_i_1(AC_reg[8]), .SHL(shl), .AC_i_1_2(AC_reg[6]), .ADD(ADD), .DR(DR),
    .\output (to_AC[7]));
  ALU_stage1 _3 (
    .AC_i(AC_reg[3]), .AND(AND), .DR_i(DR_Reg[3]), .LD(LD), .INPR(inpr), .INPR_i(INP_reg[3]), .COM(com),
    .CLK(clk), .SHR(shr), .AC_i_1(AC_reg[4]), .SHL(shl), .AC_i_1_2(AC_reg[2]), .ADD(ADD), .DR(DR),
    .\output (to_AC[3]));
  ALU_stage1 _6 (
    .AC_i(AC_reg[6]), .AND(AND), .DR_i(DR_Reg[6]), .LD(LD), .INPR(inpr), .INPR_i(INP_reg[6]), .COM(com),
    .CLK(clk), .SHR(shr), .AC_i_1(AC_reg[7]), .SHL(shl), .AC_i_1_2(AC_reg[5]), .ADD(ADD), .DR(DR),
    .\output (to_AC[6]));
  ALU_stage1 _14 (
    .AC_i(AC_reg[14]), .AND(AND), .DR_i(DR_Reg[14]), .LD(LD), .INPR(inpr), .INPR_i(undriven_4), .COM(com),
    .CLK(clk), .SHR(shr), .AC_i_1(AC_reg[15]), .SHL(shl), .AC_i_1_2(AC_reg[13]), .ADD(ADD), .DR(DR),
    .\output (to_AC[14]));
  ALU_stage1 _10 (
    .AC_i(AC_reg[10]), .AND(AND), .DR_i(DR_Reg[10]), .LD(LD), .INPR(inpr), .INPR_i(undriven_3), .COM(com),
    .CLK(clk), .SHR(shr), .AC_i_1(AC_reg[11]), .SHL(shl), .AC_i_1_2(AC_reg[9]), .ADD(ADD), .DR(DR),
    .\output (to_AC[10]));
  ALU_stage1 _2 (
    .AC_i(AC_reg[2]), .AND(AND), .DR_i(DR_Reg[2]), .LD(LD), .INPR(inpr), .INPR_i(INP_reg[2]), .COM(com),
    .CLK(clk), .SHR(shr), .AC_i_1(AC_reg[3]), .SHL(shl), .AC_i_1_2(AC_reg[1]), .ADD(ADD), .DR(DR),
    .\output (to_AC[2]));
  ALU_stage1 _13 (
    .AC_i(AC_reg[13]), .AND(AND), .DR_i(DR_Reg[13]), .LD(LD), .INPR(inpr), .INPR_i(undriven_6), .COM(com),
    .CLK(clk), .SHR(shr), .AC_i_1(AC_reg[14]), .SHL(shl), .AC_i_1_2(AC_reg[12]), .ADD(ADD), .DR(DR),
    .\output (to_AC[13]));
  ALU_stage1 _9 (
    .AC_i(AC_reg[9]), .AND(AND), .DR_i(DR_Reg[9]), .LD(LD), .INPR(inpr), .INPR_i(undriven_5), .COM(com),
    .CLK(clk), .SHR(shr), .AC_i_1(AC_reg[10]), .SHL(shl), .AC_i_1_2(AC_reg[8]), .ADD(ADD), .DR(DR),
    .\output (to_AC[9]));
  ALU_stage1 _5 (
    .AC_i(AC_reg[5]), .AND(AND), .DR_i(DR_Reg[5]), .LD(LD), .INPR(inpr), .INPR_i(INP_reg[5]), .COM(com),
    .CLK(clk), .SHR(shr), .AC_i_1(AC_reg[6]), .SHL(shl), .AC_i_1_2(AC_reg[4]), .ADD(ADD), .DR(DR),
    .\output (to_AC[5]));
  ALU_stage1 _1 (
    .AC_i(AC_reg[1]), .AND(AND), .DR_i(DR_Reg[1]), .LD(LD), .INPR(inpr), .INPR_i(INP_reg[1]), .COM(com),
    .CLK(clk), .SHR(shr), .AC_i_1(AC_reg[2]), .SHL(shl), .AC_i_1_2(AC_reg[0]), .ADD(ADD), .DR(DR),
    .\output (to_AC[1]));
  ALU_stage1 _12 (
    .AC_i(AC_reg[12]), .AND(AND), .DR_i(DR_Reg[12]), .LD(LD), .INPR(inpr), .INPR_i(undriven_7), .COM(com),
    .CLK(clk), .SHR(shr), .AC_i_1(AC_reg[13]), .SHL(shl), .AC_i_1_2(AC_reg[11]), .ADD(ADD), .DR(DR),
    .\output (to_AC[12]));
  ALU_stage1 _8 (
    .AC_i(AC_reg[8]), .AND(AND), .DR_i(DR_Reg[8]), .LD(LD), .INPR(inpr), .INPR_i(undriven_8), .COM(com),
    .CLK(clk), .SHR(shr), .AC_i_1(AC_reg[9]), .SHL(shl), .AC_i_1_2(AC_reg[7]), .ADD(ADD), .DR(DR),
    .\output (to_AC[8]));
  ALU_stage1 _4 (
    .AC_i(AC_reg[4]), .AND(AND), .DR_i(DR_Reg[4]), .LD(LD), .INPR(inpr), .INPR_i(INP_reg[4]), .COM(com),
    .CLK(clk), .SHR(shr), .AC_i_1(AC_reg[5]), .SHL(shl), .AC_i_1_2(AC_reg[3]), .ADD(ADD), .DR(DR),
    .\output (to_AC[4]));
  ALU_stage1 _0 (
    .AC_i(AC_reg[0]), .AND(AND), .DR_i(DR_Reg[0]), .LD(LD), .INPR(inpr), .INPR_i(INP_reg[0]), .COM(com),
    .CLK(clk), .SHR(shr), .AC_i_1(AC_reg[1]), .SHL(shl), .AC_i_1_2(E), .ADD(ADD), .DR(DR), .\output (to_AC[0]));

  // Other names for the same wires on the sheet: _0 = AC_reg[0]; _1 = AC_reg[1]; _2 = AC_reg[2]; _3 = AC_reg[3];
  //   _4 = AC_reg[4]; _5 = AC_reg[5]; _6 = AC_reg[6]; _7 = AC_reg[7]; _8 = AC_reg[8]; _9 = AC_reg[9];
  //   _10 = AC_reg[10]; _11 = AC_reg[11]; _12 = AC_reg[12]; _13 = AC_reg[13]; _14 = AC_reg[14]; O0 = to_AC[0];
  //   O1 = to_AC[1]; O2 = to_AC[2]; O3 = to_AC[3]; O4 = to_AC[4]; O5 = to_AC[5]; O6 = to_AC[6]; O7 = to_AC[7];
  //   O8 = to_AC[8]; O9 = to_AC[9]; O10 = to_AC[10]; O11 = to_AC[11]; O12 = to_AC[12]; O13 = to_AC[13];
  //   O14 = to_AC[14]; O15 = to_AC[15]

  // Notes on the sheet:
  //   INPR
  //   SHR
  //   SHL
  //   COM
  //   INP Reg
endmodule

module SC (
  input  B0,
  input  Clock,
  input  D7I_prime_T3,
  input  D7IT3,
  input  RT2,
  input  D0T6,
  input  D1T5,
  input  D2T6,
  input  D3T5,
  input  D4T5,
  input  D5T5,
  input  D6T6,
  output T0,
  output T1,
  output T2,
  output T3,
  output T4,
  output T5,
  output T6,
  output T7,
  output T8,
  output T9,
  output T10,
  output T11,
  output T12,
  output T13,
  output T14,
  output T15
);

  wire and_1_out, not_1_out, or_1_out;
  wire [3:0] SC_q;

  and and_1 (and_1_out, B0, D7I_prime_T3);
  Counter #(.width(4), .max('hf)) SC (
    .count(not_1_out), .Q(SC_q), .clk(Clock), .clr(or_1_out));  // open: load, D, carry
  not not_1 (not_1_out, or_1_out);
  or or_1 (or_1_out, and_1_out, D7I_prime_T3, D7IT3, RT2, D0T6, D1T5, D2T6, D3T5, D4T5, D5T5, D6T6);
  Decoder #(.select(4), .enable("false")) decoder_1 (
    .out0(T0), .out1(T1), .out2(T2), .out3(T3), .out4(T4), .out5(T5), .out6(T6), .out7(T7), .out8(T8),
    .out9(T9), .out10(T10), .out11(T11), .out12(T12), .out13(T13), .out14(T14), .out15(T15), .sel(SC_q));

  // Notes on the sheet:
  //   T1
  //   T2
  //   T4
  //   T0
  //   T5
  //   T3
  //   T12
  //   T6
  //   T10
  //   T7
  //   T8
  //   T9
  //   T13
  //   T11
  //   T14
  //   T15
endmodule
